# Fritzing sketch postit-3 contacts (saved by Fritzing 0.9.1b)
circuit board: 5.07559cm x 1.95439cm
breadboards: 1

parts:
  Q1 = NPN-Transistor [package="TO92 [THT]"]
  Q2 = NPN-Transistor [package="TO92 [THT]"]
  C1 = Electrolytic Capacitor [capacitance=22µF package="100 mil [THT, electrolytic]"]
  D1 = Rectifier Diode [part_number=1N4001 package="300 mil [THT]"]
  C2 = Electrolytic Capacitor [capacitance=1µF package="100 mil [THT, electrolytic]"]
  R1 = Resistor [tolerance=±5% resistance=10k package=THT]
  R3 = Resistor [tolerance=±5% resistance=10k package=THT]
  R4 = Resistor [tolerance=±5% resistance=1k package=THT]
  C3 = Ceramic Capacitor [capacitance=10nF package="100 mil [THT, multilayer]"]
  R5 = Resistor [tolerance=±5% resistance=10k package=THT]
  D2 = Rectifier Diode [part_number=1N4001 package="300 mil [THT]"]
  R6 = Trimmer Potentiometer [maximum_resistance=10kΩ package=THT]
  R7 = Resistor [tolerance=±5% resistance=00 package=THT]

nets:
  GND: Q1.E, Q2.E, C1.-, R5.Pin_0
  N1: Q1.B, C2.-, R6.leg2
  N2: Q1.C, R3.Pin_0, R4.Pin_1, C3.1
  N3: Q2.B, R4.Pin_0, D2.cathode
  N4: Q2.C, C2.+, R1.Pin_0
  N5: C1.+, D1.cathode, R1.Pin_1, R3.Pin_1, R7.Pin_1
  Gachette: D1.anode, D2.anode
  out: C3.0, R5.Pin_1
  N6: R6.wiper, R7.Pin_0
