# Fritzing sketch postit (saved by Fritzing 0.9.1b)
circuit board: 3.84819cm x 1.68687cm
breadboards: 1

parts:
  IC1 = General purpose bipolar Timer [package=dil-08]
  R1 = Resistor [tolerance=±5% resistance=33k package=THT]
  C1 = Ceramic Capacitor [capacitance=100nF package="100 mil [THT, multilayer]"]
  C2 = Ceramic Capacitor [capacitance=100nF package="100 mil [THT, multilayer]"]
  R2 = Resistor [tolerance=±5% resistance=4.7k package=THT]
  S1 = Pushbutton [package="[THT]"]
  R3 = Resistor [tolerance=±5% resistance=220 package=THT]
  J1 = female pin header, 2 pins [form="♀ (female)"]

nets:
  GND: IC1.GND, C1.0, R2.Pin_0, R3.Pin_0, J1.pin2
  N1: IC1.TRI, S1.Pin_1, S1.Pin_2
  N2: IC1.OUT, C2.1
  Vcc: IC1._RES, IC1.VCC+, R1.Pin_1, J1.pin1
  N3: IC1.TRE, IC1.DIS
  N4: R1.Pin_0, C1.1
  N5: C2.0, R2.Pin_1
  N6: S1.Pin_4, R3.Pin_1
