# Fritzing sketch postit2-2 (saved by Fritzing 0.9.1b)
circuit board: 5.37292cm x 1.37652cm
breadboards: 1

parts:
  IC1 = General purpose bipolar Timer [package=dil-08]
  C2 = Ceramic Capacitor [capacitance=22nF package="100 mil [THT, multilayer]"]
  R2 = Resistor [tolerance=±5% resistance=10k package=THT]
  C3 = Electrolytic Capacitor [capacitance=22µF package="100 mil [THT, electrolytic]"]
  D1 = Rectifier Diode [part_number=1N4001 package="300 mil [THT]"]
  D2 = Rectifier Diode [part_number=1N4001 package="300 mil [THT]"]
  C4 = Electrolytic Capacitor [capacitance=3.3µF voltage=50V package="100 mil [THT, electrolytic]"]
  J1 = female pin header, 3 pins [form="♀ (female)"]
  R7 = Resistor [tolerance=±5% resistance=0 package=THT]
  P1 = Trimmer Potentiometer [maximum_resistance=10kΩ package=THT]

nets:
  GND: IC1.GND, R2.Pin_0, C3.-, C4.-, J1.pin3
  Start: IC1.TRI, D1.anode, J1.pin1
  N1: IC1.OUT, C2.1
  Vcc: IC1._RES, IC1.VCC+, C3.+, D1.cathode, R7.Pin_1
  N2: IC1.TRE, IC1.DIS, C4.+, P1.wiper
  N3: C2.0, R2.Pin_1, D2.cathode
  Out: D2.anode, J1.pin2
  N4: R7.Pin_0, P1.leg1

notes:
  gnd
  Vcc
  Res
